// Logisim project fpa.circ as structural Verilog: 10 circuits, main circuit main
module main (
  input  [15:0] A,
  input  [15:0] B,
  output [15:0] res
);

  wire add_subtract_1_sign, exceptions_1_no_except, extractor_1_sa, extractor_1_sb, shift_selector_1_s_big,
       shift_selector_1_s_sml;
  wire [3:0] extractor_1_ea, extractor_1_eb, norm_exp_mant_1_ea, norm_exp_mant_1_eb,
       shift_selector_1_exp_out, shift_selector_1_shift_amt;
  wire [4:0] normalization_1_exp_out, rounding_1_exp_out;
  wire [10:0] extractor_1_fa, extractor_1_fb;
  wire [11:0] rounding_1_mant_out;
  wire [15:0] exceptions_1_res, normalization2_1_float;
  wire [19:0] norm_exp_mant_1_ma, norm_exp_mant_1_mb, normalization_1_mant_out, shift_selector_1_m_big,
       shift_selector_1_m_sml, sticky_shifter_1_m_sml_out;
  wire [20:0] add_subtract_1_mant;

  extractor extractor_1 (
    .A(A), .B(B), .sa(extractor_1_sa), .ea(extractor_1_ea), .fa(extractor_1_fa), .sb(extractor_1_sb),
    .eb(extractor_1_eb), .fb(extractor_1_fb));
  add_subtract add_subtract_1 (
    .s_big(shift_selector_1_s_big), .s_sml(shift_selector_1_s_sml), .m_big(shift_selector_1_m_big),
    .m_sml(sticky_shifter_1_m_sml_out), .sign(add_subtract_1_sign), .mant(add_subtract_1_mant));
  norm_exp_mant norm_exp_mant_1 (
    .ea_in(extractor_1_ea), .fa(extractor_1_fa), .eb_in(extractor_1_eb), .fb(extractor_1_fb),
    .ea(norm_exp_mant_1_ea), .eb(norm_exp_mant_1_eb), .ma(norm_exp_mant_1_ma), .mb(norm_exp_mant_1_mb));
  normalization normalization_1 (
    .exp(shift_selector_1_exp_out), .mant(add_subtract_1_mant), .exp_out(normalization_1_exp_out),
    .mant_out(normalization_1_mant_out));
  exceptions exceptions_1 (
    .sa(extractor_1_sa), .ea(extractor_1_ea), .fa(extractor_1_fa), .sb(extractor_1_sb), .eb(extractor_1_eb),
    .fb(extractor_1_fb), .no_except(exceptions_1_no_except), .res(exceptions_1_res));
  Multiplexer #(.width(16)) multiplexer_1 (
    .in0(exceptions_1_res), .in1(normalization2_1_float), .out(res), .sel(exceptions_1_no_except));
  shift_selector shift_selector_1 (
    .ea(norm_exp_mant_1_ea), .eb(norm_exp_mant_1_eb), .ma(norm_exp_mant_1_ma), .mb(norm_exp_mant_1_mb),
    .sa(extractor_1_sa), .sb(extractor_1_sb), .exp_out(shift_selector_1_exp_out),
    .shift_amt(shift_selector_1_shift_amt), .m_big(shift_selector_1_m_big), .m_sml(shift_selector_1_m_sml),
    .s_big(shift_selector_1_s_big), .s_sml(shift_selector_1_s_sml));
  rounding rounding_1 (
    .exp(normalization_1_exp_out), .mant(normalization_1_mant_out), .exp_out(rounding_1_exp_out),
    .mant_out(rounding_1_mant_out));
  sticky_shifter sticky_shifter_1 (
    .shift_amt(shift_selector_1_shift_amt), .m_sml(shift_selector_1_m_sml),
    .m_sml_out(sticky_shifter_1_m_sml_out));
  normalization2 normalization2_1 (
    .sign(add_subtract_1_sign), .exp(rounding_1_exp_out), .mant(rounding_1_mant_out),
    .float(normalization2_1_float));
endmodule

module extractor (
  input  [15:0] A,
  input  [15:0] B,
  output sa,
  output [3:0] ea,
  output [10:0] fa,
  output sb,
  output [3:0] eb,
  output [10:0] fb
);


  assign ea = A[14:11];
  assign eb = B[14:11];
  assign fa = A[10:0];
  assign fb = B[10:0];
  assign sa = A[15];
  assign sb = B[15];
endmodule

module norm_exp_mant (
  input  [3:0] ea_in,
  input  [10:0] fa,
  input  [3:0] eb_in,
  input  [10:0] fb,
  output [3:0] ea,
  output [3:0] eb,
  output [19:0] ma,
  output [19:0] mb
);

  or or_1 (ma[19], ea_in[0], ea_in[1], ea_in[2], ea_in[3]);
  or or_2 (mb[19], eb_in[0], eb_in[1], eb_in[2], eb_in[3]);
  Multiplexer #(.width(4)) multiplexer_1 (.in0(4'b0001), .in1(ea_in), .out(ea), .sel(ma[19]));
  Multiplexer #(.width(4)) multiplexer_2 (.in0(4'b0001), .in1(eb_in), .out(eb), .sel(mb[19]));

  assign ma[18:0] = {fa, {8{1'b0}}};
  assign mb[18:0] = {fb, {8{1'b0}}};

  // Notes on the sheet:
  //   nonzero
  //   nonzero
  //   8 guard bit
  //   8 guard bit
endmodule

module shift_selector (
  input  [3:0] ea,
  input  [3:0] eb,
  input  [19:0] ma,
  input  [19:0] mb,
  input  sa,
  input  sb,
  output [3:0] exp_out,
  output [3:0] shift_amt,
  output [19:0] m_big,
  output [19:0] m_sml,
  output s_big,
  output s_sml
);

  wire and_1_out, comparator_1_eq, comparator_1_gt, comparator_2_eq, multiplexer_1_out, multiplexer_2_out,
       not_1_out, subtractor_1_bout;
  wire [3:0] negator_1_out, subtractor_1_out;

  Comparator #(.width(20)) comparator_1 (.a(ma), .b(mb), .gt(comparator_1_gt), .eq(comparator_1_eq));  // open: lt
  Subtractor #(.width(4)) subtractor_1 (.a(ea), .b(eb), .out(subtractor_1_out), .bout(subtractor_1_bout));  // open: bin
  not not_1 (not_1_out, subtractor_1_bout);
  Comparator #(.width(4)) comparator_2 (.a(ea), .b(eb), .eq(comparator_2_eq));  // open: gt, lt
  Multiplexer multiplexer_1 (.in0(not_1_out), .in1(comparator_1_gt), .out(multiplexer_1_out), .sel(comparator_2_eq));
  and and_1 (and_1_out, comparator_2_eq, comparator_1_eq);
  Multiplexer multiplexer_2 (.in0(multiplexer_1_out), .in1(and_1_out), .out(multiplexer_2_out), .sel(and_1_out));
  Multiplexer #(.width(4)) multiplexer_3 (.in0(eb), .in1(ea), .out(exp_out), .sel(multiplexer_2_out));
  Multiplexer #(.width(20)) multiplexer_4 (.in0(mb), .in1(ma), .out(m_big), .sel(multiplexer_2_out));
  Multiplexer #(.width(20)) multiplexer_5 (.in0(ma), .in1(mb), .out(m_sml), .sel(multiplexer_2_out));
  Multiplexer multiplexer_6 (.in0(sb), .in1(sa), .out(s_big), .sel(multiplexer_2_out));
  Multiplexer multiplexer_7 (.in0(sa), .in1(sb), .out(s_sml), .sel(multiplexer_2_out));
  Negator #(.width(4)) negator_1 (.in(subtractor_1_out), .out(negator_1_out));
  Multiplexer #(.width(4)) multiplexer_8 (
    .in0(negator_1_out), .in1(subtractor_1_out), .out(shift_amt), .sel(multiplexer_2_out));

  // Notes on the sheet:
  //   a_bigger
endmodule

module sticky_shifter (
  input  [3:0] shift_amt,
  input  [19:0] m_sml,
  output [19:0] m_sml_out
);

  wire comparator_1_eq;
  wire [0:0] not_1_out;
  wire [15:0] shifter_1_out, subtractor_1_out;
  wire [19:0] and_1_out, shifter_2_out;

  Shifter #(.width(16)) shifter_1 (.in(16'h1), .\dist (shift_amt), .out(shifter_1_out));
  Shifter #(.shift("lr"), .width(20)) shifter_2 (.in(m_sml), .\dist ({1'b0, shift_amt}), .out(shifter_2_out));
  Subtractor #(.width(16)) subtractor_1 (.a(shifter_1_out), .b(16'h1), .out(subtractor_1_out));  // open: bin, bout
  assign m_sml_out = shifter_2_out | {{19{1'b0}}, not_1_out[0]};  // OR_Gate or_1, 20 bits wide
  assign and_1_out = {4'b0000, subtractor_1_out} & m_sml;  // AND_Gate and_1, 20 bits wide
  not not_1 (not_1_out[0], comparator_1_eq);
  Comparator #(.width(20)) comparator_1 (.a(and_1_out), .b({20{1'b0}}), .eq(comparator_1_eq));  // open: gt, lt

  // Notes on the sheet:
  //   sticky_bit
endmodule

module add_subtract (
  input  s_big,
  input  s_sml,
  input  [19:0] m_big,
  input  [19:0] m_sml,
  output sign,
  output [20:0] mant
);

  wire xnor_1_out;
  wire [20:0] adder_1_out, subtractor_1_out;

  xnor xnor_1 (xnor_1_out, s_big, s_sml);
  Adder #(.width(21)) adder_1 (.a({1'b0, m_big}), .b({1'b0, m_sml}), .out(adder_1_out));  // open: cin, cout
  Subtractor #(.width(21)) subtractor_1 (
    .a({1'b0, m_big}), .b({1'b0, m_sml}), .out(subtractor_1_out));  // open: bin, bout
  Multiplexer #(.width(21)) multiplexer_1 (.in0(subtractor_1_out), .in1(adder_1_out), .out(mant), .sel(xnor_1_out));

  assign sign = s_big;

  // Notes on the sheet:
  //   same_sign
endmodule

module normalization (
  input  [3:0] exp,
  input  [20:0] mant,
  output [4:0] exp_out,
  output [19:0] mant_out
);

  wire comparator_1_gt;
  wire [4:0] adder_1_out, bitfinder_1_index, multiplexer_1_out, subtractor_1_out, subtractor_2_out,
       subtractor_3_out;
  wire [20:0] or_1_out, shifter_1_out, shifter_2_out;
  wire [20:20] multiplexer_3_out;

  Shifter #(.shift("lr"), .width(21)) shifter_1 (.in(mant), .\dist (5'b00001), .out(shifter_1_out));
  BitFinder #(.\type ("high1"), .width(21)) bitfinder_1 (.in(mant), .index(bitfinder_1_index));  // open: found
  Subtractor #(.width(5)) subtractor_1 (.a({1'b0, exp}), .b(5'b00001), .out(subtractor_1_out));  // open: bin, bout
  Subtractor #(.width(5)) subtractor_2 (
    .a({1'b0, exp}), .b(multiplexer_1_out), .out(subtractor_2_out));  // open: bin, bout
  Adder #(.width(5)) adder_1 (.a({1'b0, exp}), .b(5'b00001), .out(adder_1_out));  // open: cin, cout
  assign or_1_out = shifter_1_out | {{20{1'b0}}, mant[0]};  // OR_Gate or_1, 21 bits wide
  Subtractor #(.width(5)) subtractor_3 (
    .a(5'b10011), .b(bitfinder_1_index), .out(subtractor_3_out));  // open: bin, bout
  Shifter #(.width(21)) shifter_2 (.in(mant), .\dist (multiplexer_1_out), .out(shifter_2_out));
  Comparator #(.width(5)) comparator_1 (
    .a(subtractor_3_out), .b(subtractor_1_out), .gt(comparator_1_gt));  // open: eq, lt
  Multiplexer #(.width(5)) multiplexer_1 (
    .in0(subtractor_3_out), .in1(subtractor_1_out), .out(multiplexer_1_out), .sel(comparator_1_gt));
  Multiplexer #(.width(5)) multiplexer_2 (.in0(subtractor_2_out), .in1(adder_1_out), .out(exp_out), .sel(mant[20]));
  Multiplexer #(.width(21)) multiplexer_3 (
    .in0(shifter_2_out), .in1(or_1_out), .out({multiplexer_3_out[20], mant_out}), .sel(mant[20]));

  // Notes on the sheet:
  //   overflow
  //   shift_amt
endmodule

module rounding (
  input  [4:0] exp,
  input  [19:0] mant,
  output [4:0] exp_out,
  output [11:0] mant_out
);

  wire and_1_out, or_1_out, or_2_out;
  wire [11:0] adder_2_out;
  wire [11:11] adder_2_cout;

  Adder #(.width(5)) adder_1 (.a(exp), .b({5{1'b0}}), .out(exp_out), .cin(adder_2_cout[11]));  // open: cout
  or or_1 (or_1_out, mant[0], mant[1], mant[2], mant[3], mant[4], mant[5]);
  or or_2 (or_2_out, or_1_out, mant[7], mant[8]);
  and and_1 (and_1_out, mant[6], or_2_out);
  Adder #(.width(12)) adder_2 (
    .a({12{1'b0}}), .b(mant[19:8]), .out(adder_2_out), .cin(and_1_out), .cout(adder_2_cout[11]));
  Multiplexer #(.width(12)) multiplexer_1 (
    .in0(adder_2_out), .in1({adder_2_cout[11], adder_2_out[11:1]}), .out(mant_out), .sel(adder_2_cout[11]));

  // Notes on the sheet:
  //   S
  //   G
  //   R
  //   lsb
  //   mant
  //   round_up
  //   overflow
endmodule

module normalization2 (
  input  sign,
  input  [4:0] exp,
  input  [11:0] mant,
  output [15:0] float
);

  wire comparator_1_eq, comparator_2_eq, not_1_out, or_1_out, or_2_out;
  wire [3:0] multiplexer_2_out, multiplexer_3_out;
  wire [10:0] multiplexer_1_out;

  Comparator #(.width(12)) comparator_1 (.a(mant), .b({12{1'b0}}), .eq(comparator_1_eq));  // open: gt, lt
  Multiplexer #(.width(11)) multiplexer_1 (
    .in0(mant[10:0]), .in1(mant[11:1]), .out(multiplexer_1_out), .sel(comparator_2_eq));
  Multiplexer #(.width(4)) multiplexer_2 (.in0(exp[3:0]), .in1(4'b0000), .out(multiplexer_2_out), .sel(or_2_out));
  or or_1 (or_1_out, exp[4], comparator_1_eq);
  Multiplexer #(.width(4)) multiplexer_3 (
    .in0(multiplexer_2_out), .in1(4'b1111), .out(multiplexer_3_out), .sel(exp[4]));
  Comparator #(.width(5)) comparator_2 (.a(exp), .b({5{1'b0}}), .eq(comparator_2_eq));  // open: gt, lt
  not not_1 (not_1_out, mant[11]);
  Multiplexer #(.width(11)) multiplexer_4 (
    .in0(multiplexer_1_out), .in1({11{1'b0}}), .out(float[10:0]), .sel(or_1_out));
  Multiplexer #(.width(4)) multiplexer_5 (
    .in0(multiplexer_3_out), .in1(4'b0000), .out(float[14:11]), .sel(comparator_1_eq));
  or or_2 (or_2_out, comparator_2_eq, not_1_out);

  assign float[15] = sign;

  // Notes on the sheet:
  //   overflow
  //   mant_zero
  //   exp_zero
  //   no_implicit_1
  //   subnormal
endmodule

module exceptions (
  input  sa,
  input  [3:0] ea,
  input  [10:0] fa,
  input  sb,
  input  [3:0] eb,
  input  [10:0] fb,
  output no_except,
  output [15:0] res
);

  wire and_1_out, and_2_out, and_3_out, and_4_out, and_5_out, and_6_out, and_7_out, and_8_out,
       comparator_1_eq, comparator_2_eq, comparator_3_eq, comparator_4_eq, comparator_5_eq, comparator_6_eq,
       not_1_out, not_2_out, or_1_out, or_2_out, xor_1_out;
  wire [15:0] multiplexer_1_out, multiplexer_2_out, multiplexer_3_out;

  Comparator #(.width(4)) comparator_1 (.a(ea), .b(4'b0000), .eq(comparator_1_eq));  // open: gt, lt
  Comparator #(.width(4)) comparator_2 (.a(ea), .b(4'b1111), .eq(comparator_2_eq));  // open: gt, lt
  Comparator #(.width(11)) comparator_3 (.a(fa), .b({11{1'b0}}), .eq(comparator_3_eq));  // open: gt, lt
  Comparator #(.width(4)) comparator_4 (.a(eb), .b(4'b0000), .eq(comparator_4_eq));  // open: gt, lt
  Comparator #(.width(4)) comparator_5 (.a(eb), .b(4'b1111), .eq(comparator_5_eq));  // open: gt, lt
  Comparator #(.width(11)) comparator_6 (.a(fb), .b({11{1'b0}}), .eq(comparator_6_eq));  // open: gt, lt
  Multiplexer #(.width(16)) multiplexer_1 (
    .in0({sa, ea, fa}), .in1({sb, eb, fb}), .out(multiplexer_1_out), .sel(and_1_out));
  not not_1 (not_1_out, comparator_3_eq);
  not not_2 (not_2_out, comparator_6_eq);
  Multiplexer #(.width(16)) multiplexer_2 (
    .in0(multiplexer_1_out), .in1({sa, ea, fa}), .out(multiplexer_2_out), .sel(and_8_out));
  and and_1 (and_1_out, comparator_1_eq, comparator_3_eq);
  and and_2 (and_2_out, comparator_2_eq, comparator_3_eq);
  and and_3 (and_3_out, comparator_2_eq, not_1_out);
  and and_4 (and_4_out, comparator_4_eq, comparator_6_eq);
  and and_5 (and_5_out, comparator_5_eq, comparator_6_eq);
  and and_6 (and_6_out, comparator_5_eq, not_2_out);
  Multiplexer #(.width(16)) multiplexer_3 (
    .in0(multiplexer_2_out), .in1(16'h7800), .out(multiplexer_3_out), .sel(or_2_out));
  Multiplexer #(.width(16)) multiplexer_4 (.in0(multiplexer_3_out), .in1(16'h7801), .out(res), .sel(or_1_out));
  xor xor_1 (xor_1_out, sa, sb);
  and and_7 (and_7_out, and_2_out, xor_1_out, and_5_out);
  or or_1 (or_1_out, and_3_out, and_7_out, and_6_out);
  and and_8 (and_8_out, and_4_out, and_1_out);
  or or_2 (or_2_out, and_2_out, and_5_out);
  nor nor_1 (no_except, and_1_out, or_1_out, or_2_out, and_4_out);

  // Notes on the sheet:
  //   ea_zero
  //   ea_all_1
  //   fa_zero
  //   eb_zero
  //   eb_all_1
  //   fb_zero
  //   B
  //   A
  //   a_is_zero
  //   a_is_inf
  //   a_is_NaN
  //   b_is_zero
  //   b_is_inf
  //   b_is_NaN
  //   SEL_NAN
  //   SEL_B
  //   SEL_INF
  //   SEL_A
  //   SEL_NORMAL
endmodule
